# Fritzing sketch rgb (saved by Fritzing 0.9.3b)
breadboards: 1

parts:
  U1 = ESP32S-HiLetgo [part_number=ESP32S-HiLetgo]
  IC1 = ULN2003A [package="SO16 [SMD]"]
  RGB_Strip_LED1 = RGB Strip LED  # not connected
  RGB_Strip_LED2 = RGB Strip LED  # not connected

nets:
  N1: U1.GND, IC1.Out_2
  N2: U1.GPIO21, IC1.Out_3
  N3: U1.GPIO3, IC1.Out_4

notes:
  12V
  GND

custom parts:
  ESP32S-HiLetgo: HiLetgo ESP-WROOM-32 ESP32 ESP-32S Development Board 2.4GHz Dual-Mode WiFi + Bluetooth Dual Cores Microcontroller The ESP32 integrated with Antenna switches, RF Balun, power amplifiers, low-noise amplifiers, filters, and management modules, and the entire solution occupies the least area of PCB. 2.4 GHz Wi-Fi plus Bluetooth dual-mode chip, with TSMC Ultra-low power consumption 40nm technology,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
  RGB Strip LED: A tri-color Strip LED with red, green and blue. Pin order: red - common cathode - blue - green
